# Fritzing sketch tutorial (saved by Fritzing 0.9.1b)
circuit board: 8.46667cm x 5.64444cm
breadboards: 1

parts:
  Part1 = Arduino Uno (Rev3)
  M1 = DC Motor
  Q1 = TRANSISTOR_NPN [package=to-92-ammo]
  D2 = Diode [package=diode-1n4148]
  R1 = Resistor [tolerance=±5% resistance=330 package="0805 [SMD]"]

nets:
  N1: Part1.D9_PWM, R1.Pin_1
  N2: Part1.5V, M1.pin_2, D2.A
  N3: Part1.GND, Q1.C
  N4: M1.pin_1, Q1.E, D2.C
  N5: Q1.B, R1.Pin_0
